# Fritzing sketch I2C_LCD1602 (saved by Fritzing 0.8.7b)

parts:
  module1 = I2C LCD1602
  元件1 = Arduino Uno (Rev3) - ICSP

nets:
  N1: module1.SCL, 元件1.A5/SCL
  N2: module1.SDA, 元件1.A4/SDA
  VCC: module1.VCC, 元件1.5V
  GND: module1.GND, 元件1.GND

notes:
  I2C_LCD1602

custom parts:
  I2C LCD1602: I2C LCD1602 module of SunFounder Sensor Kit
