# Fritzing sketch Gas Sensor (saved by Fritzing 0.8.7b)

parts:
  module1 = MQ-2 Gas Sensor
  元件1 = Arduino Uno (Rev3) - ICSP

nets:
  N1: module1.AO, 元件1.A0
  N2: module1.DO, 元件1.D7
  VCC: module1.VCC, 元件1.5V
  GND: module1.GND, 元件1.GND

notes:
  Gas sensor

custom parts:
  MQ-2 Gas Sensor: MQ-2 Gas Sensor module of SunFounder Sensor Kit
