# Fritzing sketch Humiture sensor (saved by Fritzing 0.8.7b)

parts:
  元件1 = Arduino Uno (Rev3) - ICSP
  module1 = DHT11 Humiture Sensor
  module2 = I2C LCD1602

nets:
  N1: 元件1.A4/SDA, module2.SDA
  N2: 元件1.A5/SCL, module2.SCL
  VCC: 元件1.5V, module1.VCC, module2.VCC
  GND: 元件1.GND, module1.GND, module2.GND
  N3: 元件1.D7, module1.SIG

notes:
  Humiture sensor

custom parts:
  DHT11 Humiture Sensor: DHT11 Humiture Sensor module of SunFounder Sensor Kit
  I2C LCD1602: I2C LCD1602 module of SunFounder Sensor Kit
