# Fritzing sketch Joystick PS2 (saved by Fritzing 0.8.7b)

parts:
  元件1 = Arduino Uno (Rev3) - ICSP
  module1 = JoyStick

nets:
  N1: 元件1.A0, module1.X
  N2: 元件1.A1, module1.Y
  GND: 元件1.GND, module1.GND
  N3: 元件1.D7, module1.BT
  5V: 元件1.5V, module1.VCC

notes:
  Joystick PS2

custom parts:
  JoyStick: JoyStick module of SunFounder Sensor Kit
