# Fritzing sketch Vibration Switch (saved by Fritzing 0.8.7b)

parts:
  元件1 = Arduino Uno (Rev3) - ICSP
  module4 = Vibration Switch

nets:
  N1: 元件1.D8, module4.SIG
  5V: 元件1.5V, module4.VCC
  GND: 元件1.GND, module4.GND

notes:
  Vibration Switch
