# Fritzing sketch Photoresistor Sensor (saved by Fritzing 0.8.7b)

parts:
  module1 = Photoresistor
  元件1 = Arduino Uno (Rev3) - ICSP
  module2 = Relay Module

nets:
  N1: module1.SIG, 元件1.A0
  GND: module1.GND, 元件1.GND, module2.GND
  VCC: module1.VCC, 元件1.5V, module2.VCC
  N2: 元件1.D8, module2.SIG

notes:
  Photoresister
  relay

custom parts:
  Photoresistor: Photoresistor module of SunFounder Sensor Kit
  Relay Module: Relay Module of SunFounder Sensor Kit
