# Fritzing sketch Reed Switch (saved by Fritzing 0.8.7b)

parts:
  module1 = Reed Switch
  元件1 = Arduino Uno (Rev3) - ICSP

nets:
  N1: module1.SIG, 元件1.D7
  GND: module1.GND, 元件1.GND
  VCC: module1.VCC, 元件1.5V

notes:
  Reed Switch

custom parts:
  Reed Switch: Reed Switch module of SunFounder Sensor Kit
