# Fritzing sketch relay (saved by Fritzing 0.8.7b)

parts:
  元件1 = Arduino Uno (Rev3) - ICSP
  module1 = Relay Module

nets:
  N1: 元件1.D7, module1.SIG
  5V: 元件1.5V, module1.VCC
  GND: 元件1.GND, module1.GND

notes:
  Relay Module

custom parts:
  Relay Module: Relay Module of SunFounder Sensor Kit
