# Fritzing sketch Controlling LED by Potentiometer (saved by Fritzing 0.8.7b)

parts:
  元件2 = Arduino Uno (Rev3) - ICSP
  module1 = Potentiometer

nets:
  N1: 元件2.A0, module1.SIG
  5V: 元件2.5V, module1.VCC
  GND: 元件2.GND, module1.GND

notes:
  Potentiometer

custom parts:
  Potentiometer: Potentiometer module of SunFounder Sensor Kit
