# Fritzing sketch Tilt_switch (saved by Fritzing 0.8.7b)

parts:
  元件1 = Arduino Uno (Rev3) - ICSP
  module1 = Tilt-Switch

nets:
  GND: 元件1.GND, module1.GND
  N1: 元件1.D7, module1.SIG
  5V: 元件1.5V, module1.VCC

notes:
  tilt_switch

custom parts:
  Tilt-Switch: Tilt-Switch module of SunFounder Sensor Kit
