# Fritzing sketch passive buzzer (saved by Fritzing 0.8.7b)

parts:
  元件1 = Arduino Uno (Rev3) - ICSP
  module1 = Buzzer

nets:
  GND: 元件1.GND, module1.GND
  N1: 元件1.D7, module1.SIG
  3V3: 元件1.3V3, module1.VCC

notes:
  Buzzer

custom parts:
  Buzzer: buzzer module of SunFounder Sensor Kit
