# Fritzing sketch Infrared-Receiver (saved by Fritzing 0.8.7b)
breadboards: 1

parts:
  元件1 = Arduino Uno (Rev3) - ICSP
  module2 = Infrared-Receiver
  R1 = Resistor [tolerance=±5% resistance=220 package=THT]
  LED1 = LED - 5mm [color="Red (633nm)" package="5 mm [THT]"]

nets:
  N1: 元件1.D13/SCK, R1.Pin_1
  GND: 元件1.GND, module2.GND, LED1.cathode
  N2: 元件1.D7, module2.SIG
  5V: 元件1.5V, module2.VCC
  N3: R1.Pin_0, LED1.anode

notes:
  Infrared-Receiver

custom parts:
  Infrared-Receiver: Infrared-Receiver module of SunFounder Sensor Kit
