# Fritzing sketch Dual-color LED (saved by Fritzing 0.8.7b)

parts:
  module1 = Double Color LED
  元件1 = Arduino Uno (Rev3) - ICSP

nets:
  N1: module1.G, 元件1.D10_PWM/SS
  GND: module1.GND, 元件1.GND
  N2: module1.R, 元件1.ICSP_MOSI, 元件1.D11_PWM/MOSI

notes:
  Dual-color LED

custom parts:
  Double Color LED: Double color LED module of SunFounder Sensor Kit
