# Fritzing sketch Sound sensor (saved by Fritzing 0.8.7b)

parts:
  元件1 = Arduino Uno (Rev3) - ICSP
  module3 = Sound Sensor

nets:
  N1: 元件1.A0, module3.SIG
  GND: 元件1.GND, module3.GND
  5V: 元件1.5V, module3.VCC

notes:
  Sound sensor

custom parts:
  Sound Sensor: Sound Sensor module of SunFounder Sensor Kit
