# Fritzing sketch Rotary Encoder (saved by Fritzing 0.8.7b)

parts:
  元件1 = Arduino Uno (Rev3) - ICSP
  module1 = Rotary Encoder

nets:
  N1: 元件1.D2, module1.CLK
  N2: 元件1.D3_PWM, module1.DT
  N3: 元件1.D4, module1.SW
  5V: 元件1.5V, module1.VCC
  GND: 元件1.GND, module1.GND

notes:
  Rotary Encoder

custom parts:
  Rotary Encoder: Rotary Encoder module of SunFounder Sensor Kit
