# Fritzing sketch Laser Transmitter (saved by Fritzing 0.8.7b)

parts:
  元件1 = Arduino Uno (Rev3) - ICSP
  module1 = Laser

nets:
  N1: 元件1.D7, module1.SIG
  5V: 元件1.5V, module1.VCC

notes:
  Laser Transmitter

custom parts:
  Laser: Laser module for SunFounder Sensor Kit
