# Fritzing sketch Hall switch sensor (saved by Fritzing 0.8.7b)

parts:
  module1 = SwitchHall sensor
  module2 = Buzzer
  元件1 = Arduino Uno (Rev3) - ICSP

nets:
  N1: module1.SIG, 元件1.D8
  GND: module1.GND, module2.GND, 元件1.GND
  VCC: module1.VCC, 元件1.5V
  N2: module2.SIG, 元件1.D7
  VCC_2: module2.VCC, 元件1.3V3

notes:
  Switch Hall
  Passive buzzer

custom parts:
  SwitchHall sensor: Switch Hall module of SunFounder Sensor Kit
  Buzzer: buzzer module of SunFounder Sensor Kit
