# Fritzing sketch Tracking (saved by Fritzing 0.8.7b)

parts:
  元件1 = Arduino Uno (Rev3) - ICSP
  module1 = Tracking

nets:
  N1: 元件1.D7, module1.SIG
  5V: 元件1.5V, module1.VCC
  GND: 元件1.GND, module1.GND

notes:
  Tracking

custom parts:
  Tracking: Tracking module of SunFounder Sensor Kit
