# Fritzing sketch Obstacle Avoidance Sensor (saved by Fritzing 0.8.7b)

parts:
  元件1 = Arduino Uno (Rev3) - ICSP
  module1 = IR Obstacle

nets:
  GND: 元件1.GND, module1.GND
  N1: 元件1.D7, module1.SIG
  5V: 元件1.5V, module1.VCC

notes:
  IR Obstacle

custom parts:
  IR Obstacle: IR Obstacle module of SunFounder Sensor Kit.
