# Fritzing sketch color sensor (saved by Fritzing 0.8.7b)

parts:
  module1 = Color Seneor
  元件1 = Arduino Uno (Rev3) - ICSP

nets:
  N1: module1.S0, 元件1.D3_PWM
  N2: module1.S1, 元件1.D4
  N3: module1.S2, 元件1.D5_PWM
  N4: module1.S3, 元件1.D6_PWM
  N5: module1.OUT, 元件1.D2
  VCC: module1.VCC, 元件1.5V
  GND: module1.GND, 元件1.GND

notes:
  color sensor

custom parts:
  Color Seneor: Color Sensor of SunFounder Sensor Kit for Arduino
