# Fritzing sketch AD DA Converter PCF8591 (saved by Fritzing 0.8.7b)

parts:
  元件1 = Arduino Uno (Rev3) - ICSP
  module1 = PCF8591

nets:
  N1: 元件1.A4/SDA, module1.SDA
  N2: 元件1.A5/SCL, module1.SCL
  N3: 元件1.D13/SCK, module1.AO
  5V: 元件1.5V, module1.VCC
  GND: 元件1.GND, module1.GND

notes:
  AD/DA Converter PCF8591

custom parts:
  PCF8591: PCF8591 ADC module for SunFounder Sensor Kit
