# Fritzing sketch Raindrop Sensor (saved by Fritzing 0.8.7b)

parts:
  元件1 = Arduino Uno (Rev3) - ICSP
  module1 = Rain Detection board
  module2 = LM393

nets:
  N1: 元件1.A0, module2.AO
  5V: 元件1.5V, module2.VCC
  N2: 元件1.D7, module2.DO
  N3: 元件1.GND, module2.GND#8
  N4: module1.+, module2.GND#10
  N5: module1.-, module2.IN

notes:
  Raindrop sensor analyser
  Raindrop Sensor

custom parts:
  Rain Detection board: Rain Detection board for SunFounder Sensor Kit (along with LM393).
  LM393: LM393 module of SunFounder Sensor Kit
