# Fritzing sketch ultrasonic (saved by Fritzing 0.8.7b)

parts:
  U1 = HC-SR04 [chip_label=IC package="SIP (Single Inline) [THT]"]
  元件1 = Arduino Uno (Rev3) - ICSP
  module1 = I2C LCD1602

nets:
  VCC: U1.Vcc, 元件1.5V, module1.VCC
  N1: U1.Trig, 元件1.D2
  N2: U1.Echo, 元件1.D3_PWM
  GND: U1.GND, 元件1.GND, module1.GND
  N3: 元件1.A4/SDA, module1.SDA
  N4: 元件1.A5/SCL, module1.SCL

notes:
  Ultrasonic sensor

custom parts:
  HC-SR04: HC-SR04 ultrasound distance sensor
  I2C LCD1602: I2C LCD1602 module of SunFounder Sensor Kit
