# Fritzing sketch Thermostatic Water Tank (saved by Fritzing 0.8.7b)
breadboards: 1

parts:
  元件1 = Arduino Uno (Rev3) - ICSP
  module1 = Relay Module
  module2 = I2C LCD1602
  module3 = Button
  module4 = Analog Thermistor
  module5 = Rotary Encoder

nets:
  N1: 元件1.A0, module4.SIG
  N2: 元件1.A4/SDA, module2.SDA
  N3: 元件1.A5/SCL, module2.SCL
  GND: 元件1.GND, module1.GND, module2.GND, module3.GND, module4.GND, module5.GND
  N4: 元件1.D10_PWM/SS, module3.SIG
  N5: 元件1.D2, module1.SIG
  N6: 元件1.D5_PWM, module5.SW
  N7: 元件1.D6_PWM, module5.DT
  N8: 元件1.D7, module5.CLK
  VCC: 元件1.5V, module1.VCC, module2.VCC, module3.VCC, module4.VCC, module5.VCC

notes:
  Thermistor
  Button
  Rotary Encoder
  Relay
  I2C LCD1602

custom parts:
  Relay Module: Relay Module of SunFounder Sensor Kit
  I2C LCD1602: I2C LCD1602 module of SunFounder Sensor Kit
  Button: Button module of SunFounder Sensor Kit
  Analog Thermistor: Analog Thermistor module of SunFounder Sensor Kit
  Rotary Encoder: Rotary Encoder module of SunFounder Sensor Kit
