# Fritzing sketch temperature Sensor (saved by Fritzing 0.8.7b)

parts:
  元件1 = Arduino Uno (Rev3) - ICSP
  module2 = Thermister

nets:
  N1: 元件1.A0, module2.AO
  GND: 元件1.GND, module2.GND
  N2: 元件1.D7, module2.DO
  5V: 元件1.5V, module2.VCC

notes:
  temperature Sensor

custom parts:
  Thermister: Thermister module of SunFounder Sensor Kit
