# Fritzing sketch auto flash led (saved by Fritzing 0.8.7b)

parts:
  元件1 = Arduino Uno (Rev3) - ICSP
  module1 = Auto Flash LED

nets:
  GND: 元件1.GND, module1.GND
  5V: 元件1.5V, module1.VCC

notes:
  Auto-flash LED

custom parts:
  Auto Flash LED: Auto Flash LED module of SunFounder Sensor Kit
