# Fritzing sketch Barometer (saved by Fritzing 0.8.7b)

parts:
  module1 = Barometer
  元件1 = Arduino Uno (Rev3) - ICSP

nets:
  N1: module1.SCL, 元件1.A5/SCL
  N2: module1.SDA, 元件1.A4/SDA
  VCC: module1.VCC, 元件1.5V
  GND: module1.GND, 元件1.GND

notes:
  Barometer

custom parts:
  Barometer: barometer module of SunFounder Sensor Kit
