# Fritzing sketch DS1302 (saved by Fritzing 0.8.7b)

parts:
  module1 = DS1302 RTC
  元件1 = Arduino Uno (Rev3) - ICSP
  module2 = I2C LCD1602

nets:
  N1: module1.SCL, 元件1.D7
  N2: module1.SDA, 元件1.D6_PWM
  VCC: module1.VCC, 元件1.5V, module2.VCC
  GND: module1.GND, 元件1.GND, module2.GND
  N3: module1.RST, 元件1.D5_PWM
  N4: 元件1.A4/SDA, module2.SDA
  N5: 元件1.A5/SCL, module2.SCL

notes:
  DS1302

custom parts:
  DS1302 RTC: DS1302RTC module of SunFounder Sensor Kit
  I2C LCD1602: I2C LCD1602 module of SunFounder Sensor Kit
