# Fritzing sketch flame sensor (saved by Fritzing 0.8.7b)

parts:
  元件1 = Arduino Uno (Rev3) - ICSP
  module1 = Flame Sensor
  module2 = Buzzer

nets:
  N1: 元件1.A0, module1.AO
  VCC: 元件1.5V, module1.VCC, module2.VCC
  N2: 元件1.D8, module1.DO
  GND: 元件1.GND, module1.GND, module2.GND
  N3: 元件1.D7, module2.SIG

notes:
  flame sensor
  passive buzzer

custom parts:
  Flame Sensor: Flame Sensor module of SunFounder Sensor Kit
  Buzzer: buzzer module of SunFounder Sensor Kit
